# Fritzing sketch TeensyUNity3Controller (saved by Fritzing 0.7.5b)
breadboards: 1

parts:
  Teensy1 = Teensy 2.0
  Part1 = Thumb Joystick
  Part2 = Triple Axis Accelerometer Breakout - ADXL335
  R1 = Rotary Potentiometer (Small) [maximum_resistance=100kΩ]
  R2 = Rotary Potentiometer (Small) [maximum_resistance=100kΩ]
  S1 = Pushbutton [package="[THT]"]
  S2 = Pushbutton [package="[THT]"]
  R3 = Resistor [tolerance=±5% resistance=10k package=THT]
  R4 = Resistor [tolerance=±5% resistance=10k package=THT]

nets:
  GND: Teensy1.GND, Part1.GND, Part2.GND, R1.leg1, R2.leg1, R3.Pin_1, R4.Pin_1
  N1: Teensy1.D0, S2.Pin_3, S2.Pin_4, R4.Pin_0
  N2: Teensy1.D1, S1.Pin_3, S1.Pin_4, R3.Pin_0
  N3: Teensy1.B6, Part1.HORZ
  N4: Teensy1.F7, Part1.VERT
  N5: Teensy1.F6, Part2.XOUT
  N6: Teensy1.F5, Part2.YOUT
  N7: Teensy1.F4, Part2.ZOUT
  N8: Teensy1.F1, R1.wiper
  N9: Teensy1.F0, R2.wiper
  VCC: Teensy1.VCC, Part1.VCC, Part2.VCC, R1.leg2, R2.leg2, S1.Pin_1, S1.Pin_2, S2.Pin_1, S2.Pin_2
